// Digital circuit 3-bit binary counter.dig as structural Verilog
module _3_bit_binary_counter (
  input  Clear,
  input  Clock,
  output Q2,
  output Q2_2,
  output Q1,
  output Q1_2,
  output Q0,
  output Q0_2
);

  wire and_1_out, and_2_out, and_3_out, and_4_out, and_5_out, and_6_out, not_1_out, or_1_out, or_2_out;

  not not_1 (not_1_out, Clear);
  and and_1 (and_1_out, not_1_out, Q2_2, Q1, Q0);
  and and_2 (and_2_out, not_1_out, Q2, Q1_2);
  and and_3 (and_3_out, not_1_out, Q2, Q0_2);
  and and_4 (and_4_out, not_1_out, Q1_2, Q0);
  and and_5 (and_5_out, not_1_out, Q1, Q0_2);
  and and_6 (and_6_out, not_1_out, Q0_2);
  or or_1 (or_1_out, and_1_out, and_2_out, and_3_out);
  or or_2 (or_2_out, and_4_out, and_5_out);
  D_FF u_Q2 (.D(or_1_out), .C(Clock), .Q(Q2), .nQ(Q2_2));
  D_FF u_Q1 (.D(or_2_out), .C(Clock), .Q(Q1), .nQ(Q1_2));
  D_FF u_Q0 (.D(and_6_out), .C(Clock), .Q(Q0), .nQ(Q0_2));

  // Other names for the same wires on the sheet: ClockLocal = Clock; Q0_t = Q0_2; Q1_t = Q1_2; Q2_t = Q2_2
endmodule

/* Test case:
Clear Clock Q2 Q2' Q1 Q1' Q0 Q0'
# T4
0 0 0 1 0 1 0 1
0 1 0 1 0 1 1 0
0 0 0 1 0 1 1 0
0 1 0 1 1 0 0 1
0 0 0 1 1 0 0 1
0 1 0 1 1 0 1 0
0 0 0 1 1 0 1 0
0 1 1 0 0 1 0 1
0 0 1 0 0 1 0 1
1 1 1 0 0 1 1 0
1 0 1 0 0 1 1 0
# T5
0 1 0 1 0 1 0 1
0 0 0 1 0 1 0 1
0 1 0 1 0 1 1 0
0 0 0 1 0 1 1 0
0 1 0 1 1 0 0 1
0 0 0 1 1 0 0 1
0 1 0 1 1 0 1 0
0 0 0 1 1 0 1 0
0 1 1 0 0 1 0 1
0 0 1 0 0 1 0 1
0 1 1 0 0 1 1 0
0 0 1 0 0 1 1 0
1 1 1 0 1 0 0 1
1 0 1 0 1 0 0 1
# T7 -> T0
0 1 0 1 0 1 0 1
0 0 0 1 0 1 0 1
0 1 0 1 0 1 1 0
0 0 0 1 0 1 1 0
0 1 0 1 1 0 0 1
0 0 0 1 1 0 0 1
0 1 0 1 1 0 1 0
0 0 0 1 1 0 1 0
0 1 1 0 0 1 0 1
0 0 1 0 0 1 0 1
0 1 1 0 0 1 1 0
0 0 1 0 0 1 1 0
0 1 1 0 1 0 0 1
0 0 1 0 1 0 0 1
0 1 1 0 1 0 1 0
0 0 1 0 1 0 1 0
0 1 0 1 0 1 0 1
*/
