// Digital circuit ALU.dig as structural Verilog
module ALU (
  input  [7:0] Pin,
  input  [7:0] DataBus,
  input  F0,
  input  F1,
  output [7:0] ALUOut,
  output Z
);

  wire Add, Bit0_cout, Bit1_cout, Bit3_2_cout, Bit3_cout, Bit4_cout, Bit5_cout, Bit6_cout, Dec, Inc,
       multiplexer_1_out, multiplexer_2_out, multiplexer_3_out, multiplexer_4_out, multiplexer_5_out,
       multiplexer_6_out, multiplexer_7_out, multiplexer_8_out, or_1_out, Sub, xor_1_out, xor_2_out,
       xor_3_out, xor_4_out, xor_5_out, xor_6_out, xor_7_out, xor_8_out;

  Decoder #(.Selector_Bits(2)) decoder_1 (.sel({F1, F0}), .out_0(Add), .out_1(Sub), .out_2(Inc), .out_3(Dec));
  or or_1 (or_1_out, Sub, Inc);
  xor xor_1 (xor_1_out, Sub, DataBus[7]);
  xor xor_2 (xor_2_out, Sub, DataBus[6]);
  xor xor_3 (xor_3_out, Sub, DataBus[5]);
  xor xor_4 (xor_4_out, Sub, DataBus[4]);
  xor xor_5 (xor_5_out, Sub, DataBus[3]);
  xor xor_6 (xor_6_out, Sub, DataBus[2]);
  xor xor_7 (xor_7_out, Sub, DataBus[1]);
  xor xor_8 (xor_8_out, Sub, DataBus[0]);
  Multiplexer multiplexer_1 (.sel(F1), .in_0(Pin[7]), .in_1(F0), .out(multiplexer_1_out));
  Multiplexer multiplexer_2 (.sel(F1), .in_0(Pin[6]), .in_1(F0), .out(multiplexer_2_out));
  Multiplexer multiplexer_3 (.sel(F1), .in_0(Pin[5]), .in_1(F0), .out(multiplexer_3_out));
  Multiplexer multiplexer_4 (.sel(F1), .in_0(Pin[4]), .in_1(F0), .out(multiplexer_4_out));
  Multiplexer multiplexer_5 (.sel(F1), .in_0(Pin[3]), .in_1(F0), .out(multiplexer_5_out));
  Multiplexer multiplexer_6 (.sel(F1), .in_0(Pin[2]), .in_1(F0), .out(multiplexer_6_out));
  Multiplexer multiplexer_7 (.sel(F1), .in_0(Pin[1]), .in_1(F0), .out(multiplexer_7_out));
  Multiplexer multiplexer_8 (.sel(F1), .in_0(Pin[0]), .in_1(F0), .out(multiplexer_8_out));
  FullAdder Bit7 (.A(multiplexer_1_out), .B(xor_1_out), .Cin(Bit6_cout), .S(ALUOut[7]));  // open: Cout
  FullAdder Bit6 (.A(multiplexer_2_out), .B(xor_2_out), .Cin(Bit5_cout), .Cout(Bit6_cout), .S(ALUOut[6]));
  FullAdder Bit5 (.A(multiplexer_3_out), .B(xor_3_out), .Cin(Bit4_cout), .Cout(Bit5_cout), .S(ALUOut[5]));
  FullAdder Bit4 (.A(multiplexer_4_out), .B(xor_4_out), .Cin(Bit3_cout), .Cout(Bit4_cout), .S(ALUOut[4]));
  FullAdder Bit3 (.A(multiplexer_5_out), .B(xor_5_out), .Cin(Bit3_2_cout), .Cout(Bit3_cout), .S(ALUOut[3]));
  FullAdder Bit3_2 (.A(multiplexer_6_out), .B(xor_6_out), .Cin(Bit1_cout), .Cout(Bit3_2_cout), .S(ALUOut[2]));
  FullAdder Bit1 (.A(multiplexer_7_out), .B(xor_7_out), .Cin(Bit0_cout), .Cout(Bit1_cout), .S(ALUOut[1]));
  FullAdder Bit0 (.A(multiplexer_8_out), .B(xor_8_out), .Cin(or_1_out), .Cout(Bit0_cout), .S(ALUOut[0]));
  nor nor_1 (Z, ALUOut[7], ALUOut[6], ALUOut[5], ALUOut[4], ALUOut[3], ALUOut[2], ALUOut[1], ALUOut[0]);

  // Other names for the same wires on the sheet: F0Local = F0; F1Local = F1; P0 = Pin[0]; P1 = Pin[1]; P2 = Pin[2];
  //   P3 = Pin[3]; P4 = Pin[4]; P5 = Pin[5]; P6 = Pin[6]; P7 = Pin[7]
endmodule

/* Test case:
Pin DataBus F1 F0 ALUOut Z
0 0 0 0 0 1
18 5 0 0 23 0
18 5 0 1 13 0
0 1 1 0 2 0
0 1 1 1 0 1
*/
