// Digital circuit Circuit.dig as structural Verilog
module Circuit (
  input  Reset,
  input  Clock
);

  wire not_1_out, simplecpu_1_read, simplecpu_1_write;
  wire [4:0] simplecpu_1_addressbus;
  wire [7:0] eeprom_1_d;

  SimpleCPU simplecpu_1 (
    .Clock(Clock), .Reset(Reset), .DataBus(eeprom_1_d), .AddressBus(simplecpu_1_addressbus),
    .Read(simplecpu_1_read), .Write(simplecpu_1_write));
  not not_1 (not_1_out, Reset);
  EEPROM #(.AddrBits(5), .isProgramMemory("true"), .Bits(8)) eeprom_1 (
    .A(simplecpu_1_addressbus), .CS(not_1_out), .WE(simplecpu_1_write), .OE(simplecpu_1_read), .D(eeprom_1_d));

  // Notes on the sheet:
  //   contents of eeprom_1 (hex, n*v repeats v):
  //   19,53,33,19,55,35,d3,13,79,33,15,79,35,b9,f0,c0,18,39,c0,b9,f7
  //   ,99,e7,d7,6,6
endmodule
