// Digital circuit ControlSignalsLogic1.dig as structural Verilog
module ControlSignalsLogic1 (
  input  Reset,
  input  Clock,
  input  Load,
  input  Store,
  input  Add,
  input  Sub,
  input  Inc,
  input  Dec,
  input  Bra,
  input  Beq,
  input  T0,
  input  T1,
  input  T2,
  input  T3,
  input  T4,
  input  T5,
  input  T6,
  input  T7,
  input  Z,
  output Read,
  output Write,
  output Cmar,
  output Cmbr,
  output Embr,
  output Cir,
  output Eir,
  output Cpc,
  output Epc,
  output Cd0,
  output Ed0,
  output Calu,
  output Ealu,
  output F0,
  output F1
);

  wire and_1_out, and_2_out, and_3_out, and_4_out, and_5_out, and_6_out, and_7_out, and_8_out, and_9_out,
       and_10_out, and_11_out, and_12_out, and_13_out, and_14_out, and_15_out, and_16_out, and_17_out,
       and_18_out, and_20_out, and_21_out, and_22_out, and_23_out, and_24_out, and_25_out, and_26_out,
       and_27_out, and_28_out, and_29_out, and_30_out, and_31_out, and_32_out, and_33_out, and_34_out,
       and_35_out, and_36_out, and_37_out, and_38_out, and_39_out, and_40_out, multiplexer_1_out, not_1_out,
       ZStored;

  Multiplexer multiplexer_1 (.sel(T6), .in_0(ZStored), .in_1(Z), .out(multiplexer_1_out));
  not not_1 (not_1_out, Clock);
  D_FF d_ff_1 (.D(multiplexer_1_out), .C(not_1_out), .Q(ZStored));  // open: nQ
  and and_1 (and_1_out, Add, T5);
  and and_2 (and_2_out, Inc, T4);
  and and_3 (and_3_out, Dec, T4);
  and and_4 (and_4_out, Sub, T5);
  and and_5 (and_5_out, Inc, T5);
  and and_6 (and_6_out, Dec, T5);
  and and_7 (and_7_out, Add, T4);
  and and_8 (and_8_out, Sub, T4);
  and and_9 (and_9_out, Add, T5);
  and and_10 (and_10_out, Sub, T5);
  and and_11 (and_11_out, Inc, T5);
  and and_12 (and_12_out, Dec, T5);
  and and_13 (and_13_out, Load, T5);
  and and_14 (and_14_out, Store, T5);
  and and_15 (and_15_out, Inc, T7);
  and and_16 (and_16_out, Dec, T7);
  and and_17 (and_17_out, Load, T4);
  and and_18 (and_18_out, Store, T4);
  and and_19 (Ed0, Store, T5);
  or or_1 (Read, T1, and_13_out, and_1_out, and_4_out, and_5_out, and_6_out);
  or or_2 (Write, and_14_out, and_15_out, and_16_out);
  or or_3 (Cmar, T0, and_17_out, and_18_out, and_7_out, and_8_out, and_2_out, and_3_out);
  or or_4 (Cmbr, and_9_out, and_10_out, and_11_out, and_12_out);
  and and_20 (and_20_out, Bra, T4);
  and and_21 (and_21_out, Beq, ZStored, T4);
  and and_22 (and_22_out, Add, T6);
  and and_23 (and_23_out, Sub, T6);
  and and_24 (and_24_out, Inc, T6);
  and and_25 (and_25_out, Dec, T6);
  and and_26 (and_26_out, Add, T4);
  and and_27 (and_27_out, Sub, T4);
  and and_28 (and_28_out, Inc, T4);
  and and_29 (and_29_out, Dec, T4);
  and and_30 (and_30_out, Bra, T4);
  and and_31 (and_31_out, T4, ZStored, Beq);
  and and_32 (and_32_out, Load, T5);
  and and_33 (and_33_out, Add, T7);
  and and_34 (and_34_out, Sub, T7);
  and and_35 (and_35_out, Load, T4);
  and and_36 (and_36_out, Store, T4);
  or or_5 (Cpc, T3, and_20_out, and_21_out);
  or or_6 (Cd0, and_32_out, and_33_out, and_34_out);
  or or_7 (Epc, T0, T2);
  or or_8 (Calu, T2, and_22_out, and_23_out, and_24_out, and_25_out);
  or or_9 (Embr, and_22_out, and_23_out, and_24_out, and_25_out);
  or or_10 (Eir, and_35_out, and_36_out, and_26_out, and_27_out, and_28_out, and_29_out, and_30_out, and_31_out);
  and and_37 (and_37_out, Add, T7);
  and and_38 (and_38_out, Sub, T7);
  and and_39 (and_39_out, Inc, T7);
  and and_40 (and_40_out, Dec, T7);
  or or_11 (Ealu, T3, and_37_out, and_38_out, and_39_out, and_40_out);
  or or_12 (F1, T2, and_24_out, and_25_out);
  or or_13 (F0, and_23_out, and_25_out);

  assign Cir = T1;

  // Other names for the same wires on the sheet: AddLocal = Add; BeqLocal = Beq; BraLocal = Bra; ClockLocal = Clock;
  //   DecLocal = Dec; IncLocal = Inc; LoadLocal = Load; ResetLocal = Reset; StoreLocal = Store; SubLocal = Sub;
  //   T0Local = T0; T1Local = T1; T2Local = T2; T3Local = T3; T4Local = T4; T5Local = T5; T6Local = T6; T7Local = T7;
  //   ZLocal = Z
endmodule
