// Digital circuit Datapath.dig as structural Verilog
module Datapath (
  input  Clock,
  input  [7:0] DataBus,
  input  Cmar,
  input  Cmbr,
  input  Embr,
  input  Cir,
  input  Eir,
  input  Cpc,
  input  Epc,
  input  Cd0,
  input  Ed0,
  input  Calu,
  input  Ealu,
  input  F0,
  input  F1,
  output [4:0] AddressBus,
  output [2:0] Opcode,
  output Z
);

  wire [4:0] IR_dataout;
  wire [7:0] alu_1_aluout, ALU_2_dataout, D0_dataout, MBR_dataout, PC_dataout;
  wire [7:5] MAR_dataout;

  Register MAR (.Datain(DataBus), .ENIn(Cmar), .Clock(Clock), .DataOut({MAR_dataout, AddressBus}));
  Register MBR (.Datain(DataBus), .ENIn(Cmbr), .Clock(Clock), .DataOut(MBR_dataout));
  Register IR (.Datain(DataBus), .ENIn(Cir), .Clock(Clock), .DataOut({Opcode, IR_dataout}));
  Register PC (.Datain(DataBus), .ENIn(Cpc), .Clock(Clock), .DataOut(PC_dataout));
  Register D0 (.Datain(DataBus), .ENIn(Cd0), .Clock(Clock), .DataOut(D0_dataout));
  ALU alu_1 (.Pin(D0_dataout), .DataBus(DataBus), .F0(F0), .F1(F1), .ALUOut(alu_1_aluout), .Z(Z));
  Register ALU_2 (.Datain(alu_1_aluout), .ENIn(Calu), .Clock(Clock), .DataOut(ALU_2_dataout));
  // Probe MAR on {MAR_dataout, AddressBus}
  assign DataBus = Embr ? MBR_dataout : 8'bz;  // Driver driver_1
  // Probe MBR on MBR_dataout
  assign DataBus = Eir ? {Opcode, IR_dataout} : 8'bz;  // Driver driver_2
  // Probe IR on {Opcode, IR_dataout}
  assign DataBus = Epc ? PC_dataout : 8'bz;  // Driver driver_3
  assign DataBus = Ed0 ? D0_dataout : 8'bz;  // Driver driver_4
  // Probe D0 on D0_dataout
  // Probe PC on PC_dataout
  assign DataBus = Ealu ? ALU_2_dataout : 8'bz;  // Driver driver_5
endmodule
