// Digital circuit InstructionSequencerFSM.dig as structural Verilog
module InstructionSequencerFSM (
  input  [2:0] Opcode,
  input  Clock,
  output T0,
  output T1,
  output T2,
  output T3,
  output T4,
  output T5,
  output T6,
  output T7,
  output Execute
);

  InstructionSequencerFSM1 instructionsequencerfsm1_1 (
    .Opcode(Opcode), .Clock(Clock), .T0(T0), .T1(T1), .T2(T2), .T3(T3), .T4(T4), .T5(T5), .T6(T6), .T7(T7),
    .Execute(Execute));
endmodule

/* Test case:
Opcode Clock T0 T1 T2 T3 T4 T5 T6 T7 Execute
#Load
0 0 1 0 0 0 0 0 0 0 0
0 1 0 1 0 0 0 0 0 0 0
0 0 0 1 0 0 0 0 0 0 0
0 1 0 0 1 0 0 0 0 0 0
0 0 0 0 1 0 0 0 0 0 0
0 1 0 0 0 1 0 0 0 0 0
0 0 0 0 0 1 0 0 0 0 0
0 1 0 0 0 0 1 0 0 0 1
0 0 0 0 0 0 1 0 0 0 1
0 1 0 0 0 0 0 1 0 0 1
0 0 0 0 0 0 0 1 0 0 1
#Store
1 1 1 0 0 0 0 0 0 0 0
1 0 1 0 0 0 0 0 0 0 0
1 1 0 1 0 0 0 0 0 0 0
1 0 0 1 0 0 0 0 0 0 0
1 1 0 0 1 0 0 0 0 0 0
1 0 0 0 1 0 0 0 0 0 0
1 1 0 0 0 1 0 0 0 0 0
1 0 0 0 0 1 0 0 0 0 0
1 1 0 0 0 0 1 0 0 0 1
1 0 0 0 0 0 1 0 0 0 1
1 1 0 0 0 0 0 1 0 0 1
1 0 0 0 0 0 0 1 0 0 1
#Add
2 1 1 0 0 0 0 0 0 0 0
2 0 1 0 0 0 0 0 0 0 0
2 1 0 1 0 0 0 0 0 0 0
2 0 0 1 0 0 0 0 0 0 0
2 1 0 0 1 0 0 0 0 0 0
2 0 0 0 1 0 0 0 0 0 0
2 1 0 0 0 1 0 0 0 0 0
2 0 0 0 0 1 0 0 0 0 0
2 1 0 0 0 0 1 0 0 0 1
2 0 0 0 0 0 1 0 0 0 1
2 1 0 0 0 0 0 1 0 0 1
2 0 0 0 0 0 0 1 0 0 1
2 1 0 0 0 0 0 0 1 0 1
2 0 0 0 0 0 0 0 1 0 1
2 1 0 0 0 0 0 0 0 1 1
2 0 0 0 0 0 0 0 0 1 1
#Sub
3 1 1 0 0 0 0 0 0 0 0
3 0 1 0 0 0 0 0 0 0 0
3 1 0 1 0 0 0 0 0 0 0
3 0 0 1 0 0 0 0 0 0 0
3 1 0 0 1 0 0 0 0 0 0
3 0 0 0 1 0 0 0 0 0 0
3 1 0 0 0 1 0 0 0 0 0
3 0 0 0 0 1 0 0 0 0 0
3 1 0 0 0 0 1 0 0 0 1
3 0 0 0 0 0 1 0 0 0 1
3 1 0 0 0 0 0 1 0 0 1
3 0 0 0 0 0 0 1 0 0 1
3 1 0 0 0 0 0 0 1 0 1
3 0 0 0 0 0 0 0 1 0 1
3 1 0 0 0 0 0 0 0 1 1
3 0 0 0 0 0 0 0 0 1 1
#Inc
4 1 1 0 0 0 0 0 0 0 0
4 0 1 0 0 0 0 0 0 0 0
4 1 0 1 0 0 0 0 0 0 0
4 0 0 1 0 0 0 0 0 0 0
4 1 0 0 1 0 0 0 0 0 0
4 0 0 0 1 0 0 0 0 0 0
4 1 0 0 0 1 0 0 0 0 0
4 0 0 0 0 1 0 0 0 0 0
4 1 0 0 0 0 1 0 0 0 1
4 0 0 0 0 0 1 0 0 0 1
4 1 0 0 0 0 0 1 0 0 1
4 0 0 0 0 0 0 1 0 0 1
4 1 0 0 0 0 0 0 1 0 1
4 0 0 0 0 0 0 0 1 0 1
4 1 0 0 0 0 0 0 0 1 1
4 0 0 0 0 0 0 0 0 1 1
#Dec
5 1 1 0 0 0 0 0 0 0 0
5 0 1 0 0 0 0 0 0 0 0
5 1 0 1 0 0 0 0 0 0 0
5 0 0 1 0 0 0 0 0 0 0
5 1 0 0 1 0 0 0 0 0 0
5 0 0 0 1 0 0 0 0 0 0
5 1 0 0 0 1 0 0 0 0 0
5 0 0 0 0 1 0 0 0 0 0
5 1 0 0 0 0 1 0 0 0 1
5 0 0 0 0 0 1 0 0 0 1
5 1 0 0 0 0 0 1 0 0 1
5 0 0 0 0 0 0 1 0 0 1
5 1 0 0 0 0 0 0 1 0 1
5 0 0 0 0 0 0 0 1 0 1
5 1 0 0 0 0 0 0 0 1 1
5 0 0 0 0 0 0 0 0 1 1
#Bra
6 1 1 0 0 0 0 0 0 0 0
6 0 1 0 0 0 0 0 0 0 0
6 1 0 1 0 0 0 0 0 0 0
6 0 0 1 0 0 0 0 0 0 0
6 1 0 0 1 0 0 0 0 0 0
6 0 0 0 1 0 0 0 0 0 0
6 1 0 0 0 1 0 0 0 0 0
6 0 0 0 0 1 0 0 0 0 0
6 1 0 0 0 0 1 0 0 0 1
6 0 0 0 0 0 1 0 0 0 1
#Beq
7 1 1 0 0 0 0 0 0 0 0
7 0 1 0 0 0 0 0 0 0 0
7 1 0 1 0 0 0 0 0 0 0
7 0 0 1 0 0 0 0 0 0 0
7 1 0 0 1 0 0 0 0 0 0
7 0 0 0 1 0 0 0 0 0 0
7 1 0 0 0 1 0 0 0 0 0
7 0 0 0 0 1 0 0 0 0 0
7 1 0 0 0 0 1 0 0 0 1
7 0 0 0 0 0 1 0 0 0 1
*/
