// Digital circuit InstructionSequencerFSM1.dig as structural Verilog
module InstructionSequencerFSM1 (
  input  [2:0] Opcode,
  input  Clock,
  output T0,
  output T1,
  output T2,
  output T3,
  output T4,
  output T5,
  output T6,
  output T7,
  output Execute
);

  wire _3_bit_binary_counter_1_q0, _3_bit_binary_counter_1_q0_2, _3_bit_binary_counter_1_q1,
       _3_bit_binary_counter_1_q1_2, _3_bit_binary_counter_1_q2, _3_bit_binary_counter_1_q2_2,
       clearlogic_1_clear;

  ClearLogic clearlogic_1 (.Opcode(Opcode), .T4(T4), .T5(T5), .Clear(clearlogic_1_clear));
  _3_bit_binary_counter _3_bit_binary_counter_1 (
    .Clear(clearlogic_1_clear), .Clock(Clock), .Q2(_3_bit_binary_counter_1_q2),
    .Q2_2(_3_bit_binary_counter_1_q2_2), .Q1(_3_bit_binary_counter_1_q1),
    .Q1_2(_3_bit_binary_counter_1_q1_2), .Q0(_3_bit_binary_counter_1_q0), .Q0_2(_3_bit_binary_counter_1_q0_2));
  OutputLogic outputlogic_1 (
    .Q2(_3_bit_binary_counter_1_q2), .Q2_2(_3_bit_binary_counter_1_q2_2), .Q1(_3_bit_binary_counter_1_q1),
    .Q1_2(_3_bit_binary_counter_1_q1_2), .Q0(_3_bit_binary_counter_1_q0),
    .Q0_2(_3_bit_binary_counter_1_q0_2), .T0(T0), .T1(T1), .T2(T2), .T3(T3), .T4(T4), .T5(T5), .T6(T6),
    .T7(T7), .Execute(Execute));

  // Other names for the same wires on the sheet: T4Local = T4; T5Local = T5
endmodule
