// Digital circuit OpcodeDecoder.dig as structural Verilog
module OpcodeDecoder (
  input  [2:0] Opcode,
  input  Execute,
  output Load,
  output Store,
  output Add,
  output Sub,
  output Inc,
  output Dec,
  output Bra,
  output Beq
);

  OpcodeDecoder1 opcodedecoder1_1 (
    .Opcode(Opcode), .Execute(Execute), .Load(Load), .Store(Store), .Add(Add), .Sub(Sub), .Inc(Inc),
    .Dec(Dec), .Bra(Bra), .Beq(Beq));
endmodule

/* Test case:
# Input Test Vectors
# Input: Opcode, Execute
# Output: Load, Store, Add, Sub, Inc, Dec, Bra, Beq
Opcode Execute Load Store Add Sub Inc Dec Bra Beq
0 0 0 0 0 0 0 0 0 0
0 1 1 0 0 0 0 0 0 0
1 0 0 0 0 0 0 0 0 0
1 1 0 1 0 0 0 0 0 0
2 0 0 0 0 0 0 0 0 0
2 1 0 0 1 0 0 0 0 0
3 0 0 0 0 0 0 0 0 0
3 1 0 0 0 1 0 0 0 0
4 0 0 0 0 0 0 0 0 0
4 1 0 0 0 0 1 0 0 0
5 0 0 0 0 0 0 0 0 0
5 1 0 0 0 0 0 1 0 0
6 0 0 0 0 0 0 0 0 0
6 1 0 0 0 0 0 0 1 0
7 0 0 0 0 0 0 0 0 0
7 1 0 0 0 0 0 0 0 1
*/
