// Digital circuit OpcodeDecoder1.dig as structural Verilog
module OpcodeDecoder1 (
  input  [2:0] Opcode,
  input  Execute,
  output Load,
  output Store,
  output Add,
  output Sub,
  output Inc,
  output Dec,
  output Bra,
  output Beq
);

  wire and_1_out, and_2_out, and_3_out, and_4_out, and_5_out, and_6_out, and_7_out, and_8_out, not_1_out,
       not_2_out, not_3_out;

  not not_1 (not_1_out, Opcode[2]);
  not not_2 (not_2_out, Opcode[1]);
  not not_3 (not_3_out, Opcode[0]);
  and and_1 (and_1_out, not_3_out, not_2_out, not_1_out);
  and and_2 (and_2_out, Opcode[0], not_2_out, not_1_out);
  and and_3 (and_3_out, not_3_out, Opcode[1], not_1_out);
  and and_4 (and_4_out, Opcode[0], Opcode[1], not_1_out);
  and and_5 (and_5_out, not_3_out, not_2_out, Opcode[2]);
  and and_6 (and_6_out, Opcode[0], not_2_out, Opcode[2]);
  and and_7 (and_7_out, not_3_out, Opcode[1], Opcode[2]);
  and and_8 (and_8_out, Opcode[0], Opcode[1], Opcode[2]);
  and and_9 (Load, Execute, and_1_out);
  and and_10 (Store, Execute, and_2_out);
  and and_11 (Add, Execute, and_3_out);
  and and_12 (Sub, Execute, and_4_out);
  and and_13 (Inc, Execute, and_5_out);
  and and_14 (Dec, Execute, and_6_out);
  and and_15 (Bra, Execute, and_7_out);
  and and_16 (Beq, Execute, and_8_out);
endmodule
