// Digital circuit SimpleCPU.dig as structural Verilog
module SimpleCPU (
  input  Clock,
  input  Reset,
  input  [7:0] DataBus,
  output [4:0] AddressBus,
  output Read,
  output Write
);

  wire controlsignalslogic_1_calu, controlsignalslogic_1_cd0, controlsignalslogic_1_cir,
       controlsignalslogic_1_cmar, controlsignalslogic_1_cmbr, controlsignalslogic_1_cpc,
       controlsignalslogic_1_ealu, controlsignalslogic_1_ed0, controlsignalslogic_1_eir,
       controlsignalslogic_1_embr, controlsignalslogic_1_epc, controlsignalslogic_1_f0,
       controlsignalslogic_1_f1, controlsignalslogic_1_write, datapath_1_z,
       instructionsequencerfsm_1_execute, instructionsequencerfsm_1_t0, instructionsequencerfsm_1_t1,
       instructionsequencerfsm_1_t2, instructionsequencerfsm_1_t3, instructionsequencerfsm_1_t4,
       instructionsequencerfsm_1_t5, instructionsequencerfsm_1_t6, instructionsequencerfsm_1_t7, not_1_out,
       opcodedecoder_1_add, opcodedecoder_1_beq, opcodedecoder_1_bra, opcodedecoder_1_dec,
       opcodedecoder_1_inc, opcodedecoder_1_load, opcodedecoder_1_store, opcodedecoder_1_sub;
  wire [2:0] datapath_1_opcode;

  InstructionSequencerFSM instructionsequencerfsm_1 (
    .Opcode(datapath_1_opcode), .Clock(Clock), .T0(instructionsequencerfsm_1_t0),
    .T1(instructionsequencerfsm_1_t1), .T2(instructionsequencerfsm_1_t2), .T3(instructionsequencerfsm_1_t3),
    .T4(instructionsequencerfsm_1_t4), .T5(instructionsequencerfsm_1_t5), .T6(instructionsequencerfsm_1_t6),
    .T7(instructionsequencerfsm_1_t7), .Execute(instructionsequencerfsm_1_execute));
  OpcodeDecoder opcodedecoder_1 (
    .Opcode(datapath_1_opcode), .Execute(instructionsequencerfsm_1_execute), .Load(opcodedecoder_1_load),
    .Store(opcodedecoder_1_store), .Add(opcodedecoder_1_add), .Sub(opcodedecoder_1_sub),
    .Inc(opcodedecoder_1_inc), .Dec(opcodedecoder_1_dec), .Bra(opcodedecoder_1_bra), .Beq(opcodedecoder_1_beq));
  ControlSignalsLogic controlsignalslogic_1 (
    .Reset(Reset), .Clock(Clock), .Load(opcodedecoder_1_load), .Store(opcodedecoder_1_store),
    .Add(opcodedecoder_1_add), .Sub(opcodedecoder_1_sub), .Inc(opcodedecoder_1_inc),
    .Dec(opcodedecoder_1_dec), .Bra(opcodedecoder_1_bra), .Beq(opcodedecoder_1_beq),
    .T0(instructionsequencerfsm_1_t0), .T1(instructionsequencerfsm_1_t1), .T2(instructionsequencerfsm_1_t2),
    .T3(instructionsequencerfsm_1_t3), .T4(instructionsequencerfsm_1_t4), .T5(instructionsequencerfsm_1_t5),
    .T6(instructionsequencerfsm_1_t6), .T7(instructionsequencerfsm_1_t7), .Z(datapath_1_z), .Read(Read),
    .Write(controlsignalslogic_1_write), .Cmar(controlsignalslogic_1_cmar),
    .Cmbr(controlsignalslogic_1_cmbr), .Embr(controlsignalslogic_1_embr), .Cir(controlsignalslogic_1_cir),
    .Eir(controlsignalslogic_1_eir), .Cpc(controlsignalslogic_1_cpc), .Epc(controlsignalslogic_1_epc),
    .Cd0(controlsignalslogic_1_cd0), .Ed0(controlsignalslogic_1_ed0), .Calu(controlsignalslogic_1_calu),
    .Ealu(controlsignalslogic_1_ealu), .F0(controlsignalslogic_1_f0), .F1(controlsignalslogic_1_f1));
  Datapath datapath_1 (
    .Clock(Clock), .DataBus(DataBus), .Cmar(controlsignalslogic_1_cmar), .Cmbr(controlsignalslogic_1_cmbr),
    .Embr(controlsignalslogic_1_embr), .Cir(controlsignalslogic_1_cir), .Eir(controlsignalslogic_1_eir),
    .Cpc(controlsignalslogic_1_cpc), .Epc(controlsignalslogic_1_epc), .Cd0(controlsignalslogic_1_cd0),
    .Ed0(controlsignalslogic_1_ed0), .Calu(controlsignalslogic_1_calu), .Ealu(controlsignalslogic_1_ealu),
    .F0(controlsignalslogic_1_f0), .F1(controlsignalslogic_1_f1), .AddressBus(AddressBus),
    .Opcode(datapath_1_opcode), .Z(datapath_1_z));
  not not_1 (not_1_out, Clock);
  and and_1 (Write, controlsignalslogic_1_write, not_1_out);
endmodule
