// Digital circuit Solution1.dig as structural Verilog
module Solution1 (
  input  Reset,
  input  Clock
);

  wire addressdecoder_1_cs0, addressdecoder_1_cs1, simplecpu_1_read, simplecpu_1_write;
  wire [4:0] simplecpu_1_addressbus;
  wire [7:0] eeprom_1_d, portregister_1_dataout;

  SimpleCPU simplecpu_1 (
    .Clock(Clock), .Reset(Reset), .DataBus(eeprom_1_d), .AddressBus(simplecpu_1_addressbus),
    .Read(simplecpu_1_read), .Write(simplecpu_1_write));
  AddressDecoder addressdecoder_1 (
    .AddressBus(simplecpu_1_addressbus), .CS0(addressdecoder_1_cs0), .CS1(addressdecoder_1_cs1));
  EEPROM #(.AddrBits(5), .isProgramMemory("true"), .Bits(8)) eeprom_1 (
    .A(simplecpu_1_addressbus), .CS(addressdecoder_1_cs1), .WE(simplecpu_1_write), .OE(simplecpu_1_read),
    .D(eeprom_1_d));
  PortRegister portregister_1 (
    .Read(simplecpu_1_read), .Write(simplecpu_1_write), .CS(addressdecoder_1_cs0), .DataBus(eeprom_1_d),
    .DataOut(portregister_1_dataout));
  Seven_Seg_Hex seven_seg_hex_1 (.d(portregister_1_dataout[7:4]), .dp(1'b0));
  Seven_Seg_Hex seven_seg_hex_2 (.d(portregister_1_dataout[3:0]), .dp(1'b0));

  // Notes on the sheet:
  //   contents of eeprom_1 (hex, n*v repeats v):
  //   18,3f,9f,19,7f,e7,c2,bf,1f,5f,e0,c7,13*0,a
endmodule
